# Fritzing sketch Luminosità regorabile (saved by Fritzing 0.9.3b)
breadboards: 1

parts:
  Componente1 = Arduino Uno (Rev3)  # not connected
  LCD1 = LCD screen
  R1 = Trimmer Potentiometer [maximum_resistance=10kΩ package=THT]
  R2 = Resistor [tolerance=±5% resistance=220 package=THT]
  Q1 = NPN-Transistor [package="TO92 [THT]"]
  R3 = Rotary Potentiometer (Small) [maximum_resistance=100kΩ package=THT]

nets:
  N1: LCD1.VSS, LCD1.RS, R1.leg1, Q1.E, R3.leg1
  N2: LCD1.VDD, LCD1.LED+, R1.leg2, R3.leg2
  N3: LCD1.V0, R1.wiper
  N4: LCD1.LED-, Q1.C
  N5: R2.Pin_1, Q1.B
